# Fritzing sketch TempUmidity (saved by Fritzing 0.9.2b)
circuit board: 6.88566cm x 5.36311cm
breadboards: 1

parts:
  PCB1 = Arduino Shield PCB  # not connected
  LCD1 = LCD screen
  R2 = Resistor [tolerance=±5% resistance=220 package=THT]
  Contrast1 = Rotary Potentiometer (Small) [maximum_resistance=100kΩ package=THT]
  Arduino1 = Arduino Uno (Rev3)
  RHT1 = Humidity and Temperature Sensor RHT03
  R3 = Resistor [tolerance=±5% resistance=10k package=THT]

nets:
  VSS: LCD1.VSS, LCD1.R/W, LCD1.LED-, Contrast1.leg1, Arduino1.GND, RHT1.GND_2
  VDD: LCD1.VDD, R2.Pin_1, Contrast1.leg2, Arduino1.5V, RHT1.Vcc, R3.Pin_1
  N1: LCD1.V0, Contrast1.wiper
  N2: LCD1.RS, Arduino1.D12/MISO
  N3: LCD1.E, Arduino1.D11_PWM/MOSI
  N4: LCD1.DB4, Arduino1.D5_PWM
  N5: LCD1.DB5, Arduino1.D4
  N6: LCD1.DB6, Arduino1.D3_PWM
  N7: LCD1.DB7, Arduino1.D2
  N8: LCD1.LED+, R2.Pin_0
  N9: Arduino1.D6_PWM, RHT1.Data-signal, R3.Pin_0

custom parts:
  Arduino Shield PCB: Plain PCB Shaped to fit an Arduino "Shield"
